// Logisim project main.circ as structural Verilog: 4 circuits, main circuit main
module main (
  input  [1:0] RegSelecter,
  input  Opcode,
  output [15:0] Output
);

  wire control_unit_1_alu_sel;
  wire [15:0] registers_1_regout;

  Registers registers_1 (.RegSelector(RegSelecter), .RegOut(registers_1_regout));
  Control_Unit control_unit_1 (.Opcode(Opcode), .AlU_Sel(control_unit_1_alu_sel));
  Simple_ALU simple_alu_1 (.A(16'h4), .B(registers_1_regout), .ALU_sel(control_unit_1_alu_sel), .Result(Output));
endmodule

module Simple_ALU (
  input  [15:0] A,
  input  [15:0] B,
  input  ALU_sel,
  output [15:0] Result
);

  wire [15:0] adder_1_out, and_1_out;

  assign and_1_out = A & B;  // AND_Gate and_1, 16 bits wide
  Adder #(.width(16)) adder_1 (.a(A), .b(B), .out(adder_1_out), .cin(1'b0));  // open: cout
  Multiplexer #(.width(16)) multiplexer_1 (
    .in0(adder_1_out), .in1(and_1_out), .out(Result), .sel(ALU_sel));  // open: en
endmodule

module Registers (
  input  [1:0] RegSelector,
  output [15:0] RegOut
);

  wire clock_1_out, clock_2_out, clock_3_out, clock_4_out;
  wire [15:0] R0_q, R1_q, R2_q, R3_q;

  Clock clock_1 (.out(clock_1_out));
  Clock clock_2 (.out(clock_2_out));
  Clock clock_3 (.out(clock_3_out));
  Clock clock_4 (.out(clock_4_out));
  Register #(.width(16)) R0 (.D(16'h1), .Q(R0_q), .clk(clock_1_out));  // open: en, clr
  Register #(.width(16)) R1 (.D(16'h2), .Q(R1_q), .clk(clock_2_out));  // open: en, clr
  Register #(.width(16)) R2 (.D(16'h3), .Q(R2_q), .clk(clock_3_out));  // open: en, clr
  Register #(.width(16)) R3 (.D(16'h4), .Q(R3_q), .clk(clock_4_out));  // open: en, clr
  Multiplexer #(.select(2), .width(16)) multiplexer_1 (
    .in0(R0_q), .in1(R1_q), .in2(R2_q), .in3(R3_q), .out(RegOut), .sel(RegSelector));  // open: en
endmodule

module Control_Unit (
  input  Opcode,
  output AlU_Sel
);


  assign AlU_Sel = Opcode;
endmodule
